// Logisim project BC.circ as structural Verilog: 9 circuits, main circuit main
module main (
  input  in_1,
  output [7:0] out_2,
  output [7:0] out_3,
  output [7:0] out_4,
  output [3:0] out_5,
  output [7:0] out_6
);

  wire and_1_out, clock_1_out, clu_1_x1, clu_1_x2, clu_1_x3, clu_1_x4, clu_1_x5, clu_1_x6, clu_1_x7,
       clu_1_x8, clu_1_x12, clu_1_x13, not_1_out, or_1_out;
  wire [1:0] clu_1_x9, clu_1_x10, clu_1_x11;
  wire [3:0] ir_1_ir_c, mar_1_q;
  wire [7:0] alu_1_q, ir_1_ir_0, multiplexer_1_out, multiplexer_2_out, multiplexer_3_out, multiplexer_4_out;

  IR ir_1 (.D(out_6), .LOAD(clu_1_x1), .IR_C(ir_1_ir_c), .IR_0(ir_1_ir_0));
  PC pc_1 (.I(out_4), .INC(clu_1_x13), .LOAD(clu_1_x3), .O(out_2));
  CLU clu_1 (
    .T(out_5), .INSTR(ir_1_ir_c), .x1(clu_1_x1), .x2(clu_1_x2), .x3(clu_1_x3), .x4(clu_1_x4), .x5(clu_1_x5),
    .x6(clu_1_x6), .x7(clu_1_x7), .x8(clu_1_x8), .x9(clu_1_x9), .x10(clu_1_x10), .x11(clu_1_x11),
    .x12(clu_1_x12), .x13(clu_1_x13));
  Multiplexer #(.select(2), .width(8)) multiplexer_1 (
    .in0(out_2), .in1(ir_1_ir_0), .in2(out_6), .out(multiplexer_1_out), .sel(clu_1_x10));  // open: in3
  MAR mar_1 (.D(multiplexer_1_out), .LOAD(clu_1_x4), .Q(mar_1_q));
  Multiplexer #(.select(2), .width(8)) multiplexer_2 (
    .in0(out_6), .in1(ir_1_ir_0), .in2(out_2), .in3(alu_1_q), .out(multiplexer_2_out), .sel(clu_1_x11));
  T t_1 (.CLOCK_IN(clock_1_out), .HALT(in_1), .CLEAR(clu_1_x6), .T_OUT(out_5));
  not not_1 (not_1_out, clock_1_out);
  and and_1 (and_1_out, not_1_out, clock_1_out);
  MBR mbr_1 (.D(multiplexer_3_out), .LOAD(clu_1_x2), .Q(out_6));
  Multiplexer #(.width(8)) multiplexer_3 (.in0(out_3), .in1(out_4), .out(multiplexer_3_out), .sel(clu_1_x7));
  AC ac_1 (.LOAD(clu_1_x12), .D(multiplexer_2_out), .Q(out_4));
  ALU alu_1 (.D(multiplexer_4_out), .CONTROL(clu_1_x9), .Q(alu_1_q));
  Clock clock_1 (.out(clock_1_out));
  or or_1 (or_1_out, clu_1_x5, and_1_out);
  Multiplexer #(.width(8)) multiplexer_4 (.in0(out_6), .in1(out_4), .out(multiplexer_4_out), .sel(clu_1_x8));
  RAM #(.addrWidth(4)) ram_1 (.addr(mar_1_q), .we(clu_1_x5), .clk(or_1_out), .din(out_6), .dout(out_3));  // open: oe
endmodule

module T (
  input  CLOCK_IN,
  input  HALT,
  input  CLEAR,
  output [3:0] T_OUT
);

  wire and_1_out, not_1_out;
  wire [3:0] adder_1_out;

  not not_1 (not_1_out, HALT);
  Adder #(.width(4)) adder_1 (.a(T_OUT), .b(4'b0001), .out(adder_1_out));  // open: cin, cout
  Register #(.width(4)) register_1 (.D(adder_1_out), .en(and_1_out), .clk(and_1_out), .Q(T_OUT), .clr(CLEAR));
  and and_1 (and_1_out, CLOCK_IN, not_1_out);
endmodule

module PC (
  input  [7:0] I,
  input  INC,
  input  LOAD,
  output [7:0] O
);

  wire not_1_out, not_2_out, or_1_out;
  wire [7:0] adder_1_out, multiplexer_1_out;

  Adder adder_1 (.a(O), .b(8'h1), .out(adder_1_out));  // open: cin, cout
  Multiplexer #(.width(8)) multiplexer_1 (.in0(adder_1_out), .in1(I), .out(multiplexer_1_out), .sel(LOAD));
  or or_1 (or_1_out, INC, LOAD);
  not not_1 (not_1_out, or_1_out);
  not not_2 (not_2_out, not_1_out);
  Register register_1 (.D(multiplexer_1_out), .en(not_2_out), .clk(not_2_out), .Q(O));  // open: clr
endmodule

module MAR (
  input  [7:0] D,
  input  LOAD,
  output [3:0] Q
);

  wire not_1_out, not_2_out, not_3_out, not_4_out;
  wire [7:4] register_1_q;

  not not_1 (not_1_out, LOAD);
  not not_2 (not_2_out, not_1_out);
  not not_3 (not_3_out, not_2_out);
  Register register_1 (.D(D), .en(not_4_out), .clk(not_4_out), .Q({register_1_q, Q}));  // open: clr
  not not_4 (not_4_out, not_3_out);
endmodule

module IR (
  input  [7:0] D,
  input  LOAD,
  output [7:0] IR_0,
  output [3:0] IR_C
);

  Register register_1 (.D(D), .en(LOAD), .clk(LOAD), .Q({IR_C, IR_0[3:0]}));  // open: clr

  assign IR_0[7:4] = 4'b0000;
endmodule

module MBR (
  input  [7:0] D,
  input  LOAD,
  output [7:0] Q
);

  wire not_1_out, not_2_out, not_3_out, not_4_out;

  not not_1 (not_1_out, LOAD);
  not not_2 (not_2_out, not_1_out);
  not not_3 (not_3_out, not_2_out);
  not not_4 (not_4_out, not_3_out);
  Register register_1 (.D(D), .en(not_4_out), .clk(not_4_out), .Q(Q));  // open: clr
endmodule

module AC (
  input  [7:0] D,
  input  LOAD,
  output [7:0] Q
);

  wire not_1_out, not_2_out, not_3_out, not_4_out;

  not not_1 (not_1_out, LOAD);
  not not_2 (not_2_out, not_1_out);
  not not_3 (not_3_out, not_2_out);
  not not_4 (not_4_out, not_3_out);
  Register register_1 (.D(D), .en(not_4_out), .clk(not_4_out), .Q(Q));  // open: clr
endmodule

module ALU (
  input  [7:0] D,
  input  [1:0] CONTROL,
  output [7:0] Q
);

  wire and_1_out, and_2_out, not_1_out, not_2_out, not_3_out, not_4_out, not_5_out, not_6_out, or_1_out;
  wire [7:0] adder_1_out, multiplexer_1_out;

  Adder adder_1 (.a(D), .b(Q), .out(adder_1_out));  // open: cin, cout
  Multiplexer #(.select(2), .width(8)) multiplexer_1 (
    .in1(D), .in2(adder_1_out), .out(multiplexer_1_out), .sel(CONTROL));  // open: in0, in3
  not not_1 (not_1_out, CONTROL[0]);
  and and_1 (and_1_out, not_1_out, CONTROL[0]);
  and and_2 (and_2_out, CONTROL[1], not_2_out);
  not not_2 (not_2_out, CONTROL[1]);
  or or_1 (or_1_out, and_1_out, and_2_out);
  not not_3 (not_3_out, or_1_out);
  not not_4 (not_4_out, not_3_out);
  Register AD (.D(multiplexer_1_out), .clk(not_6_out), .Q(Q));  // open: en, clr
  not not_5 (not_5_out, not_4_out);
  not not_6 (not_6_out, not_5_out);
endmodule

module CLU (
  input  [3:0] T,
  input  [3:0] INSTR,
  output x1,
  output x2,
  output x3,
  output x4,
  output x5,
  output x6,
  output x7,
  output x8,
  output [1:0] x9,
  output [1:0] x10,
  output [1:0] x11,
  output x12,
  output x13
);

  ROM #(.dataWidth(16)) rom_1 (.addr({INSTR, T}), .data({x13, x12, x11, x10, x9, x8, x7, x6, x5, x4, x3, x2, x1}));

  // Notes on the sheet:
  //   contents of rom_1 (hex, n*v repeats v):
  //   8 2 1 8020 12*0 8 2 1 408 2 4000 8020 9*0 8 2 1 408 2 808 2 4000 8020 7*0 8 2 1 42 408 10 8020 9*0 8
  //   2 1 408 2 808 42 4000 10 8020 6*0 8 2 1 408 2 100 280 7000 8020 23*0 8 2 1 6000 180 5000 280 7000 4
  //   20
endmodule
