// Logisim project SC.circ as structural Verilog
module RS_Flip_Flop (
  input  R,
  input  S,
  output Q
);

  wire nand_2_out;

  nand nand_1 (Q, R, nand_2_out);
  nand nand_2 (nand_2_out, Q, S);
endmodule

module Memory_Cell (
  input  R_W,
  input  D,
  input  S,
  output Q
);

  wire nand_1_out, nand_2_out, not_1_out, not_2_out, rs_flip_flop_1_q;

  not not_1 (not_1_out, R_W);
  not not_2 (not_2_out, D);
  nand nand_1 (nand_1_out, not_1_out, D, S);
  nand nand_2 (nand_2_out, not_1_out, not_2_out, S);
  RS_Flip_Flop rs_flip_flop_1 (.R(nand_1_out), .S(nand_2_out), .Q(rs_flip_flop_1_q));
  and and_1 (Q, R_W, rs_flip_flop_1_q, S);
endmodule

module Register_8_Bit (
  input  [7:0] D,
  input  LOAD,
  output [7:0] Q
);

  Register_4_Bit register_4_bit_1 (.D(D[3:0]), .LOAD(LOAD), .Q(Q[3:0]));
  Register_4_Bit register_4_bit_2 (.D(D[7:4]), .LOAD(LOAD), .Q(Q[7:4]));
endmodule

module Register_1_Bit (
  input  D,
  input  LOAD,
  output Q
);

  wire nand_1_out, nand_2_out, not_1_out;

  not not_1 (not_1_out, D);
  nand nand_1 (nand_1_out, LOAD, D);
  nand nand_2 (nand_2_out, LOAD, not_1_out);
  RS_Flip_Flop rs_flip_flop_1 (.R(nand_1_out), .S(nand_2_out), .Q(Q));
endmodule

module Register_4_Bit (
  input  [3:0] D,
  input  LOAD,
  output [3:0] Q
);

  Register_1_Bit register_1_bit_1 (.D(D[0]), .LOAD(LOAD), .Q(Q[0]));
  Register_1_Bit register_1_bit_2 (.D(D[1]), .LOAD(LOAD), .Q(Q[1]));
  Register_1_Bit register_1_bit_3 (.D(D[2]), .LOAD(LOAD), .Q(Q[2]));
  Register_1_Bit register_1_bit_4 (.D(D[3]), .LOAD(LOAD), .Q(Q[3]));
endmodule

module Register_8_Bit_Dual (
  input  [7:0] D,
  input  LOAD,
  output [3:0] Q1,
  output [3:0] Q2
);

  Register_8_Bit register_8_bit_1 (.D(D), .LOAD(LOAD), .Q({Q2, Q1}));
endmodule

module Mplxr_4x1 (
  input  D0,
  input  D1,
  input  D2,
  input  D3,
  input  [1:0] S,
  output Q
);

  wire and_1_out, and_2_out, and_3_out, and_4_out, not_1_out, not_2_out;

  not not_1 (not_1_out, S[1]);
  not not_2 (not_2_out, S[0]);
  and and_1 (and_1_out, D0, not_1_out, not_2_out);
  and and_2 (and_2_out, D1, not_1_out, S[0]);
  and and_3 (and_3_out, D2, S[1], not_2_out);
  and and_4 (and_4_out, D3, S[1], S[0]);
  or or_1 (Q, and_1_out, and_2_out, and_3_out, and_4_out);
endmodule

module Mplxr_4x1_4_Bit (
  input  [3:0] D0,
  input  [3:0] D1,
  input  [3:0] D2,
  input  [3:0] D3,
  input  [1:0] S,
  output [3:0] Q
);

  Mplxr_4x1 mplxr_4x1_1 (.D0(D0[0]), .D1(D1[0]), .D2(D2[0]), .D3(D3[0]), .S(S), .Q(Q[0]));
  Mplxr_4x1 mplxr_4x1_2 (.D0(D0[1]), .D1(D1[1]), .D2(D2[1]), .D3(D3[1]), .S(S), .Q(Q[1]));
  Mplxr_4x1 mplxr_4x1_3 (.D0(D0[2]), .D1(D1[2]), .D2(D2[2]), .D3(D3[2]), .S(S), .Q(Q[2]));
  Mplxr_4x1 mplxr_4x1_4 (.D0(D0[3]), .D1(D1[3]), .D2(D2[3]), .D3(D3[3]), .S(S), .Q(Q[3]));
endmodule

module Mplxr_4x1_8_Bit (
  input  [7:0] D0,
  input  [7:0] D1,
  input  [7:0] D2,
  input  [7:0] D3,
  input  [1:0] S,
  output [7:0] Q
);

  Mplxr_4x1_4_Bit mplxr_4x1_4_bit_1 (.D0(D0[3:0]), .D1(D1[3:0]), .D2(D2[3:0]), .D3(D3[3:0]), .S(S), .Q(Q[3:0]));
  Mplxr_4x1_4_Bit mplxr_4x1_4_bit_2 (.D0(D0[7:4]), .D1(D1[7:4]), .D2(D2[7:4]), .D3(D3[7:4]), .S(S), .Q(Q[7:4]));
endmodule

module Mplxr_2x1 (
  input  D0,
  input  D1,
  input  S,
  output Q
);

  wire and_1_out, and_2_out, not_1_out;

  and and_1 (and_1_out, D0, not_1_out);
  not not_1 (not_1_out, S);
  and and_2 (and_2_out, D1, S);
  or or_1 (Q, and_1_out, and_2_out);
endmodule

module Mplxr_2x1_2_Bit (
  input  [1:0] D0,
  input  [1:0] D1,
  input  S,
  output [1:0] Q
);

  Mplxr_2x1 mplxr_2x1_1 (.D0(D0[0]), .D1(D1[0]), .S(S), .Q(Q[0]));
  Mplxr_2x1 mplxr_2x1_2 (.D0(D0[1]), .D1(D1[1]), .S(S), .Q(Q[1]));
endmodule

module Mplxr_2x1_4_Bit (
  input  [3:0] D0,
  input  [3:0] D1,
  input  S,
  output [3:0] out_4
);

  Mplxr_2x1_2_Bit mplxr_2x1_2_bit_1 (.D0(D0[1:0]), .D1(D1[1:0]), .S(S), .Q(out_4[1:0]));
  Mplxr_2x1_2_Bit mplxr_2x1_2_bit_2 (.D0(D0[3:2]), .D1(D1[3:2]), .S(S), .Q(out_4[3:2]));
endmodule

module Mplxr_2x1_8_Bit (
  input  [7:0] D0,
  input  [7:0] D1,
  input  in_3,
  output [7:0] Q
);

  Mplxr_2x1_4_Bit mplxr_2x1_4_bit_1 (.D0(D0[3:0]), .D1(D1[3:0]), .S(in_3), .out_4(Q[3:0]));
  Mplxr_2x1_4_Bit mplxr_2x1_4_bit_2 (.D0(D0[7:4]), .D1(D1[7:4]), .S(in_3), .out_4(Q[7:4]));
endmodule

module Dec_4x16 (
  input  [3:0] D,
  output B0,
  output B1,
  output B2,
  output B3,
  output B4,
  output B5,
  output B6,
  output B7,
  output B8,
  output B9,
  output B10,
  output B11,
  output B12,
  output B13,
  output B14,
  output B15
);

  wire not_1_out, not_2_out, not_3_out, not_4_out;

  not not_1 (not_1_out, D[0]);
  not not_2 (not_2_out, D[1]);
  not not_3 (not_3_out, D[2]);
  not not_4 (not_4_out, D[3]);
  and and_1 (B0, not_1_out, not_2_out, not_3_out, not_4_out);
  and and_2 (B1, D[0], not_2_out, not_3_out, not_4_out);
  and and_3 (B2, not_1_out, D[1], not_3_out, not_4_out);
  and and_4 (B3, D[0], D[1], not_3_out, not_4_out);
  and and_5 (B4, not_1_out, not_2_out, D[2], not_4_out);
  and and_6 (B5, D[0], not_2_out, D[2], not_4_out);
  and and_7 (B6, not_1_out, D[1], D[2], not_4_out);
  and and_8 (B7, D[0], D[1], D[2], not_4_out);
  and and_9 (B8, not_1_out, not_2_out, not_3_out, D[3]);
  and and_10 (B9, D[0], not_2_out, not_3_out, D[3]);
  and and_11 (B10, not_1_out, D[1], not_3_out, D[3]);
  and and_12 (B11, D[0], D[1], not_3_out, D[3]);
  and and_13 (B12, not_1_out, not_2_out, D[2], D[3]);
  and and_14 (B13, D[0], not_2_out, D[2], D[3]);
  and and_15 (B14, not_1_out, D[1], D[2], D[3]);
  and and_16 (B15, D[0], D[1], D[2], D[3]);
endmodule

module Add (
  input  A,
  input  B,
  input  C_IN,
  output SUM,
  output C_OUT
);

  wire and_1_out, and_2_out, xor_1_out;

  xor xor_1 (xor_1_out, A, B);
  and and_1 (and_1_out, A, B);
  and and_2 (and_2_out, xor_1_out, C_IN);
  xor xor_2 (SUM, xor_1_out, C_IN);
  or or_1 (C_OUT, and_2_out, and_1_out);
endmodule

module Add_2_Bit (
  input  [1:0] A,
  input  [1:0] B,
  input  C_IN,
  output [1:0] SUM,
  output C_OUT
);

  wire add_1_c_out;

  Add add_1 (.A(A[0]), .B(B[0]), .C_IN(C_IN), .SUM(SUM[0]), .C_OUT(add_1_c_out));
  Add add_2 (.A(A[1]), .B(B[1]), .C_IN(add_1_c_out), .SUM(SUM[1]), .C_OUT(C_OUT));
endmodule

module Add_4_Bit (
  input  [3:0] A,
  input  [3:0] B,
  input  C_IN,
  output [3:0] SUM,
  output C_OUT
);

  wire add_2_bit_1_c_out;

  Add_2_Bit add_2_bit_1 (.A(A[1:0]), .B(B[1:0]), .C_IN(C_IN), .SUM(SUM[1:0]), .C_OUT(add_2_bit_1_c_out));
  Add_2_Bit add_2_bit_2 (.A(A[3:2]), .B(B[3:2]), .C_IN(add_2_bit_1_c_out), .SUM(SUM[3:2]), .C_OUT(C_OUT));
endmodule

module Add_8_Bit (
  input  [7:0] A,
  input  [7:0] B,
  input  C_IN,
  output [7:0] SUM,
  output C_OUT
);

  wire add_4_bit_1_c_out;

  Add_4_Bit add_4_bit_1 (.A(A[3:0]), .B(B[3:0]), .C_IN(C_IN), .SUM(SUM[3:0]), .C_OUT(add_4_bit_1_c_out));
  Add_4_Bit add_4_bit_2 (.A(A[7:4]), .B(B[7:4]), .C_IN(add_4_bit_1_c_out), .SUM(SUM[7:4]), .C_OUT(C_OUT));
endmodule

module T (
  input  in_1,
  input  in_2,
  output [3:0] out_3
);

  wire and_1_out, clock_1_out, not_1_out, not_2_out, not_3_out;
  wire [3:0] add_4_bit_1_sum;

  Clock clock_1 (.out(clock_1_out));
  not not_1 (not_1_out, clock_1_out);
  not not_2 (not_2_out, not_1_out);
  not not_3 (not_3_out, not_2_out);
  and and_1 (and_1_out, clock_1_out, in_1, not_3_out);
  Register_4_Bit_Clear register_4_bit_clear_1 (.D(add_4_bit_1_sum), .LOAD(and_1_out), .CLR(in_2), .Q(out_3));
  Add_4_Bit add_4_bit_1 (.A(out_3), .B(4'b0001), .SUM(add_4_bit_1_sum));  // open: C_IN, C_OUT
endmodule

module Register_1_Bit_Clear (
  input  D,
  input  LOAD,
  input  CLR,
  output Q
);

  wire and_1_out, nand_1_out, nand_2_out, not_1_out, not_2_out, or_1_out, or_2_out;

  not not_1 (not_1_out, CLR);
  not not_2 (not_2_out, D);
  and and_1 (and_1_out, not_1_out, D);
  or or_1 (or_1_out, CLR, LOAD);
  or or_2 (or_2_out, not_2_out, CLR);
  nand nand_1 (nand_1_out, and_1_out, or_1_out);
  nand nand_2 (nand_2_out, or_1_out, or_2_out);
  RS_Flip_Flop rs_flip_flop_1 (.R(nand_1_out), .S(nand_2_out), .Q(Q));
endmodule

module Register_4_Bit_Clear (
  input  [3:0] D,
  input  LOAD,
  input  CLR,
  output [3:0] Q
);

  Register_1_Bit_Clear register_1_bit_clear_1 (.D(D[0]), .LOAD(LOAD), .CLR(CLR), .Q(Q[0]));
  Register_1_Bit_Clear register_1_bit_clear_2 (.D(D[1]), .LOAD(LOAD), .CLR(CLR), .Q(Q[1]));
  Register_1_Bit_Clear register_1_bit_clear_3 (.D(D[2]), .LOAD(LOAD), .CLR(CLR), .Q(Q[2]));
  Register_1_Bit_Clear register_1_bit_clear_4 (.D(D[3]), .LOAD(LOAD), .CLR(CLR), .Q(Q[3]));
endmodule
